# Fritzing sketch Architect_tis (saved by Fritzing 0.9.3b)
breadboards: 1

parts:
  부품1 = Arduino Uno (Rev3)
  Mod1 = KY-015 Temperature & Humidity Sensor Module [package="Breakout board"]
  Disp1 = LBT2088AH [part_number=LBT2088AH]
  U1 = MAX7219 [package=dil24]
  Driver1 = 28BYJ-48 Driver Module [part_number=ULN2003 package=THT]
  SM1 = 28BYJ-48 Stepper Motor [part_number=28BYJ-48]
  R1 = Resistor [tolerance=±5% resistance=10k package=THT]

nets:
  N1: 부품1.D10_PWM/SS, U1.DIG6
  N2: 부품1.D11_PWM/MOSI, U1.DIG4
  N3: 부품1.D13/SCK, U1.GND
  N4: 부품1.D2, Driver1.IN4
  N5: 부품1.D3_PWM, Driver1.IN3
  N6: 부품1.D4, Driver1.IN2
  N7: 부품1.D5_PWM, Driver1.IN1
  N8: 부품1.D6_PWM, Mod1.S
  5V: 부품1.5V, Mod1.Vin, U1.DIN, Driver1.Vmotor
  GND: 부품1.GND, Mod1.-, U1.DIG2, Driver1.GND, R1.Pin_0
  N9: Disp1.pin1, U1.DOUT
  N10: Disp1.pin2, U1.SEGD
  N11: Disp1.pin_3, U1.SEGDP
  N12: Disp1.pin_4, U1.SEGE
  N13: Disp1.pin_5, U1.SEGC
  N14: Disp1.pin_6, U1.VCC
  N15: Disp1.pin_7, U1.ISET
  N16: Disp1.pin_8, U1.SEGG
  N17: U1.DIG0, R1.Pin_1
  N18: Driver1.blue-pin, SM1.blue-pin
  N19: Driver1.pink-pin, SM1.pink-pin
  N20: Driver1.yellow-pin, SM1.yellow-pin
  N21: Driver1.orange-pin, SM1.orange-pin
  N22: Driver1.red-pin, SM1.red-pin

custom parts:
  KY-015 Temperature & Humidity Sensor Module: KY-015 temperature and humidity sensor module, provides a low-latency serial interface to measure humidity and temperature.
  28BYJ-48 Driver Module: ULN2003 Driver Module for the 28BYJ-48 Unipolar Stepper Motor LED A - Blue wire - Bottom coil left LED B - Pink wire - Top coil left LED C - Yellow wire - Bottom coil right LED D - Orange wire - Top coil right Common rail - red Connector pins: blue - pink - yellow - orange - red Control pins - IN1 to IN4 Power pins - GND & Vmotor (5-12V) On/Off jumper (if removed, power to motor is cut).
  28BYJ-48 Stepper Motor: Unipolar Stepper Motor 28BYJ-48 Top coil - pink & orange Bottom coil - blue & yellow Common rail - red Connector pins: blue - pink - yellow - orange - red

// code stored in the sketch: Untitled.ino
#include "DHT.h"
#include <LedControl.h>

// DHT11 ?? ??
#define DHTPIN 6        // DHT ?? ?
#define DHTTYPE DHT11   // DHT11 ?? ??

// ?? ?? ??? ??
const int motorPin1 = 5;    // IN1
const int motorPin2 = 4;    // IN2
const int motorPin3 = 3;    // IN3
const int motorPin4 = 2;    // IN4

// MAX7219 ???? LED ? ??
#define DIN 11
#define CLK 13
#define CS 10

LedControl lc = LedControl(DIN, CLK, CS, 1);

// ?? ??? ?? ??
const int steps[] = {B1000, B1100, B0100, B0110, B0010, B0011, B0001, B1001, B0000};

// ?? ?? ?? ??
const int stepsPerRevolution = 2048;  // ? ?? ??? ??? ?? ? (?? ??? ?? ?? ? ??)
const int stepsFor180 = stepsPerRevolution / 2;  // 180? ??? ??? ?? ?
int currentPosition = 0;  // ?? ?? ??
int motorSpeed = 1000;    // ?? ??? ????(?????)
bool isAt180 = false;     // 180? ?? ??? ??

DHT dht(DHTPIN, DHTTYPE);  // DHT ?? ???

void setup() {
  // ?? ???? ???? ??
  pinMode(motorPin1, OUTPUT);
  pinMode(motorPin2, OUTPUT);
  pinMode(motorPin3, OUTPUT);
  pinMode(motorPin4, OUTPUT);

  // ???? LED ???
  lc.shutdown(0, false);   // LED ???
  lc.setIntensity(0, 8);   // ?? ?? (0~15)
  lc.clearDisplay(0);      // ???

  Serial.begin(9600);
  Serial.println("DHT11, Stepper Motor, and Matrix LED Test");
  dht.begin();
}

void loop() {
  // ?? ??
  float h = dht.readHumidity();

  // ?? ???? ???? ??? ?? ??
  if (isnan(h)) {
    Serial.println("Failed to read from DHT sensor!");
    return;
  }

  // ?? ??
  Serial.print("Humidity: ");
  Serial.print(h);
  Serial.println(" %");

  // ??? 60% ??? ? 180?? ??
  if (h > 60 && !isAt180) {
    Serial.println("Motor: Rotating to 180 degrees");
    rotateTo180();
    isAt180 = true;
    displaySmileyFace(); // 180?? ? ^^ ??
  }
  // ??? 60% ??? ? 0?? ??
  else if (h <= 60 && isAt180) {
    Serial.println("Motor: Returning to 0 degrees");
    returnToZero();
    isAt180 = false;
    lc.clearDisplay(0); // 0?? ?? ? LED ???
  }

  delay(2000); // 2??? ?? ?? ??
}

// 180? ??? ??
void rotateTo180() {
  for (int i = 0; i < stepsFor180; i++) {
    clockwise();
  }
  currentPosition = stepsFor180;
}

// 0? ??? ??
void returnToZero() {
  for (int i = 0; i < stepsFor180; i++) {
    counterClockwise();
  }
  currentPosition = 0;
}

// ? ?? ?? ?? ??
void clockwise() {
  for (int i = 7; i >= 0; i--) {
    motorSignalOutput(i);
    delayMicroseconds(motorSpeed);
  }
}

// ? ?? ??? ?? ??
void counterClockwise() {
  for (int i = 0; i < 8; i++) {
    motorSignalOutput(i);
    delayMicroseconds(motorSpeed);
  }
}

// ?? ??
void motorStop() {
  motorSignalOutput(8); // 8?? ??(B0000)? ???? ??
}

// ?? ?? ?? ??
void motorSignalOutput(int out) {
  digitalWrite(motorPin1, bitRead(steps[out], 0));
  digitalWrite(motorPin2, bitRead(steps[out], 1));
  digitalWrite(motorPin4, bitRead(steps[out], 3));
}

// ???? LED? ^^ ??
void displaySmileyFace() {
  // ? ???? ?? (^^ ??)
  byte smileyFace[8] = {
    B00100100, // ^    ^
    B01000010, //  ^  ^
    B01000010, //  ^  ^
    B00000000, //
    B00000000, //
    B01000010, //  ^  ^
    B00111100, //   ^^
    B00000000  //
  };

  // ????? ??
  for (int i = 0; i < 8; i++) {
    lc.setRow(0, i, smileyFace[i]);
  }
}
